// Logisim project buttons_input_one_column_testing.circ as structural Verilog: 1 circuit, main circuit main
module main (
  output [31:0] out_1
);

  wire and_2_out, cdm_16_1_p2, cdm_16_1_p3, cdm_16_1_p5, cdm_16_1_p6, cdm_16_1_p7, cdm_16_1_p8, cdm_16_1_p9,
       change, Clock, column_needed, comparator_1_eq, comparator_2_eq, comparator_3_eq, half, mem, not_1_out,
       rd, word, x_glow, x_rise, y_glow, y_needed, y_rise;
  wire [4:0] buttons_shift_calculation_1_y_coordinate;
  wire [6:0] cdm_16_1_p14;
  wire [8:0] cdm_16_1_p14_2;
  wire [15:0] addr, cdm_16_1_p15, controlled_buffer_1_out, controlled_buffer_3_out, data, first_changed,
       half_in, y_shift;
  wire [31:0] multiplexer_4_out, multiplexer_5_out;

  Button button_1 (.out(x_glow));
  Button button_2 (.out(y_rise));
  Button button_3 (.out(change));
  Button button_4 (.out(y_glow));
  Clock clock_1 (.out(Clock));
  // Debugger debugger_1: pin names not known
  Button button_5 (.out(x_rise));
  // RAM ram_1: pin names not known; wires that end beside it: addr, word, mem, Clock, rd, data
  buttons_shift_calculation buttons_shift_calculation_1 (
    .y_coordinate(buttons_shift_calculation_1_y_coordinate), .x_rise(x_rise), .x_glow(x_glow),
    .y_rise(y_rise), .y_glow(y_glow));  // open: x_coordinate
  // Probe on cdm_16_1_p2
  // Probe on cdm_16_1_p3
  // Probe on cdm_16_1_p6
  // Probe on cdm_16_1_p5
  // CdM_16 cdm_16_1: pin names not known; wires that end beside it: 1'b1, cdm_16_1_p2, cdm_16_1_p3, Clock, cdm_16_1_p5, cdm_16_1_p6, cdm_16_1_p7, cdm_16_1_p8, cdm_16_1_p9, mem, rd, word, addr, {cdm_16_1_p14_2, cdm_16_1_p14}, cdm_16_1_p15
  // Probe on buttons_shift_calculation_1_y_coordinate
  // Probe on cdm_16_1_p7
  assign y_shift = {{11{1'b0}}, buttons_shift_calculation_1_y_coordinate};  // Bit_Extender bit_extender_1
  // Probe on cdm_16_1_p9
  // Probe on cdm_16_1_p8
  Comparator #(.width(16), .mode("unsigned")) comparator_1 (
    .a(addr), .b(16'hbeef), .eq(comparator_1_eq));  // open: gt, lt
  Comparator #(.width(16), .mode("unsigned")) comparator_2 (
    .a(addr), .b(16'hbabe), .eq(comparator_2_eq));  // open: gt, lt
  Comparator #(.width(16)) comparator_3 (.a(addr), .b(16'hbabe), .eq(comparator_3_eq));  // open: gt, lt
  Multiplexer #(.select(2), .width(16), .enable("false")) multiplexer_1 (
    .in0(controlled_buffer_3_out), .in1(y_shift), .in2(half_in), .out(cdm_16_1_p15),
    .sel({column_needed, y_needed}));  // open: in3
  and and_1 (column_needed, rd, mem, change, comparator_2_eq);
  and and_2 (and_2_out, ~rd, mem, word, comparator_3_eq);  // AND_Gate
  and and_3 (y_needed, rd, mem, change, comparator_1_eq);
  assign controlled_buffer_1_out = and_2_out ? {cdm_16_1_p14_2, cdm_16_1_p14} : 16'bz;  // Controlled_Buffer controlled_buffer_1
  TTY tty_1 ();  // open: data, clk, we, clr
  Comparator #(.width(16), .mode("unsigned")) comparator_4 (.a(y_shift), .b(16'h7), .lt(half));  // open: gt, eq
  Multiplexer #(.width(16), .enable("false")) multiplexer_2 (
    .in0(half_in), .in1(controlled_buffer_1_out), .out(first_changed), .sel(not_1_out));
  not not_1 (not_1_out, rd);
  assign data = not_1_out ? {cdm_16_1_p14_2, cdm_16_1_p14} : 16'bz;  // Controlled_Buffer controlled_buffer_2
  assign controlled_buffer_3_out = rd ? data : 16'bz;  // Controlled_Buffer controlled_buffer_3
  Multiplexer #(.width(16), .enable("false")) multiplexer_3 (
    .in0(out_1[31:16]), .in1(out_1[15:0]), .out(half_in), .sel(half));
  Multiplexer #(.width(32), .enable("false")) multiplexer_4 (
    .in0({first_changed, out_1[15:0]}), .in1({out_1[31:16], first_changed}), .out(multiplexer_4_out),
    .sel(half));
  Multiplexer #(.width(32), .enable("false")) multiplexer_5 (
    .in0(out_1), .in1(multiplexer_4_out), .out(multiplexer_5_out), .sel(change));
  Register #(.width(32)) register_1 (.D(multiplexer_5_out), .Q(out_1), .clk(Clock));  // open: en, clr
  DotMatrix #(.matrixcols(1), .matrixrows(32)) dotmatrix_1 (.col0(out_1));

  // Other names for the same wires on the sheet: _0_15[15:0] = out_1[15:0]; column_1[31:0] = out_1;
  //   second_changed[31:0] = {first_changed, out_1[15:0]}; output[15:0] = first_changed; _16_31[15:0] = out_1[31:16];
  //   first_changed[31:16] = out_1[31:16]
endmodule
