// Logisim project simplest_scheme.circ as structural Verilog: 1 circuit, main circuit main
module main (
);

  wire cdm_16_1_p1, cdm_16_1_p2, cdm_16_1_p3, Clock, mem, not_1_out, rd, word;
  wire [15:0] addr, cdm_16_1_p8, data, debugger_1_p2;

  Clock clock_1 (.out(Clock));
  // Probe on cdm_16_1_p1
  // Probe on cdm_16_1_p3
  // Probe on cdm_16_1_p2
  // CdM_16 cdm_16_1: pin names not known; wires that end beside it: cdm_16_1_p1, cdm_16_1_p2, cdm_16_1_p3, mem, rd, word, addr, cdm_16_1_p8
  // Debugger debugger_1: pin names not known; wires that end beside it: Clock, debugger_1_p2
  not not_1 (not_1_out, rd);
  assign data = not_1_out ? cdm_16_1_p8 : 16'bz;  // Controlled_Buffer controlled_buffer_1
  assign debugger_1_p2 = rd ? data : 16'bz;  // Controlled_Buffer controlled_buffer_2
  // RAM ram_1: pin names not known; wires that end beside it: addr, word, mem, Clock, rd, data
endmodule
